# Fritzing sketch Binaeruhr (saved by Fritzing 0.9.3b)
breadboards: 1

parts:
  U1 = 74HC595 [package="DIP16 [THT]"]
  U2 = 74HC595 [package="DIP16 [THT]"]
  U3 = 74HC595 [package="DIP16 [THT]"]
  Taster = Pushbutton [package="[THT]"]
  Vin = Screw terminal - 2 pins [package=THT]
  LEDH1 = LED - 5mm [color="Red (633nm)" package="5 mm [THT]"]
  LEDM1 = LED - 5mm [color="Red (633nm)" package="5 mm [THT]"]
  LEDS1 = LED - 5mm [color="Red (633nm)" package="5 mm [THT]"]
  LEDS2 = LED - 5mm [color="Red (633nm)" package="5 mm [THT]"]
  LEDS3 = LED - 5mm [color="Red (633nm)" package="5 mm [THT]"]
  LEDS4 = LED - 5mm [color="Red (633nm)" package="5 mm [THT]"]
  LEDS5 = LED - 5mm [color="Red (633nm)" package="5 mm [THT]"]
  LEDS6 = LED - 5mm [color="Red (633nm)" package="5 mm [THT]"]
  LEDH2 = LED - 5mm [color="Red (633nm)" package="5 mm [THT]"]
  LEDH3 = LED - 5mm [color="Red (633nm)" package="5 mm [THT]"]
  LEDH4 = LED - 5mm [color="Red (633nm)" package="5 mm [THT]"]
  LEDH5 = LED - 5mm [color="Red (633nm)" package="5 mm [THT]"]
  LEDM2 = LED - 5mm [color="Red (633nm)" package="5 mm [THT]"]
  LEDM3 = LED - 5mm [color="Red (633nm)" package="5 mm [THT]"]
  LEDM4 = LED - 5mm [color="Red (633nm)" package="5 mm [THT]"]
  LEDM5 = LED - 5mm [color="Red (633nm)" package="5 mm [THT]"]
  LEDM6 = LED - 5mm [color="Red (633nm)" package="5 mm [THT]"]
  Bauteil1 = Arduino Nano (Rev3.0)
  ZS-042_RTC1 = ZS-042 RTC Module
  tickled = LED - 5mm [color="Red (633nm)" package="5 mm [THT]"]

nets:
  N1: U1.Q1, LEDH2.anode
  N2: U1.Q2, LEDH3.anode
  N3: U1.Q3, LEDH4.anode
  N4: U1.Q4, LEDH5.anode
  GND: U1.GND, U1.OE, U2.GND, U2.OE, U3.GND, U3.OE, Taster.Pin_1, Taster.Pin_2, Vin.pin1, LEDH1.cathode, LEDM1.cathode, LEDS1.cathode, LEDS2.cathode, LEDS3.cathode, LEDS4.cathode, LEDS5.cathode, LEDS6.cathode, LEDH2.cathode, LEDH3.cathode, LEDH4.cathode, LEDH5.cathode, LEDM2.cathode, LEDM3.cathode, LEDM4.cathode, LEDM5.cathode, LEDM6.cathode, Bauteil1.GND, ZS-042_RTC1.GND, tickled.cathode
  5V: U1.MR, U1.VCC, U2.MR, U2.VCC, U3.MR, U3.VCC, Bauteil1.5V, ZS-042_RTC1.VCC
  N5: U1.SH_CP, Bauteil1.D10
  N6: U1.ST_CP, Bauteil1.D9
  N7: U1.DS, Bauteil1.D8
  N8: U1.Q0, LEDH1.anode
  N9: U2.Q1, LEDM2.anode
  N10: U2.Q2, LEDM3.anode
  N11: U2.Q3, LEDM4.anode
  N12: U2.Q4, LEDM5.anode
  N13: U2.Q5, LEDM6.anode
  N14: U2.SH_CP, Bauteil1.D7
  N15: U2.ST_CP, Bauteil1.D6
  N16: U2.DS, Bauteil1.D5
  N17: U2.Q0, LEDM1.anode
  N18: U3.Q1, LEDS2.anode
  N19: U3.Q2, LEDS3.anode
  N20: U3.Q3, LEDS4.anode
  N21: U3.Q4, LEDS5.anode
  N22: U3.Q5, LEDS6.anode
  N23: U3.SH_CP, Bauteil1.D4
  N24: U3.ST_CP, Bauteil1.D3
  N25: U3.DS, Bauteil1.D2
  N26: U3.Q0, LEDS1.anode
  N27: Taster.Pin_3, Bauteil1.D12/MISO
  N28: Vin.pin2, Bauteil1.VIN
  N29: Bauteil1.A5, ZS-042_RTC1.SCL
  N30: Bauteil1.A4, ZS-042_RTC1.SDA
  N31: Bauteil1.D13/SCK, tickled.anode

notes:
  Stunden
  Minuten
  Sekunden
