# Fritzing sketch Binaeruhr_Platine (saved by Fritzing 0.9.3b)
circuit board: 8.51628cm x 5.04089cm
breadboards: 1

parts:
  U1 = 74HC595 [package="DIP16 [THT]"]
  U2 = 74HC595 [package="DIP16 [THT]"]
  U3 = 74HC595 [package="DIP16 [THT]"]
  Vin = Screw terminal - 2 pins [package=THT]
  Bauteil1 = Arduino Nano (Rev3.0)
  ZS-042_RTC1 = ZS-042 RTC Module
  Tick_Taster = female pin header, 2 pins [form="♀ (female)"]
  Stunden = female pin header, 5 pins [form="♀ (female)"]
  Minuten = female pin header, 6 pins [form="♀ (female)"]
  Senkunden = female pin header, 6 pins [form="♀ (female)"]

nets:
  N1: U1.Q1, Stunden.pin2
  N2: U1.Q2, Stunden.pin3
  N3: U1.Q3, Stunden.pin4
  N4: U1.Q4, Stunden.pin5
  GND: U1.GND, U1.OE, U2.GND, U2.OE, U3.GND, U3.OE, Vin.pin1, Bauteil1.GND, ZS-042_RTC1.GND
  5V: U1.MR, U1.VCC, U2.MR, U2.VCC, U3.MR, U3.VCC, Bauteil1.5V, ZS-042_RTC1.VCC
  N5: U1.SH_CP, Bauteil1.D10
  N6: U1.ST_CP, Bauteil1.D9
  N7: U1.DS, Bauteil1.D8
  N8: U1.Q0, Stunden.pin1
  N9: U2.Q1, Minuten.pin2
  N10: U2.Q2, Minuten.pin3
  N11: U2.Q3, Minuten.pin4
  N12: U2.Q4, Minuten.pin5
  N13: U2.Q5, Minuten.pin6
  N14: U2.SH_CP, Bauteil1.D7
  N15: U2.ST_CP, Bauteil1.D6
  N16: U2.DS, Bauteil1.D5
  N17: U2.Q0, Minuten.pin1
  N18: U3.Q1, Senkunden.pin2
  N19: U3.Q2, Senkunden.pin3
  N20: U3.Q3, Senkunden.pin4
  N21: U3.Q4, Senkunden.pin5
  N22: U3.Q5, Senkunden.pin6
  N23: U3.SH_CP, Bauteil1.D4
  N24: U3.ST_CP, Bauteil1.D3
  N25: U3.DS, Bauteil1.D2
  N26: U3.Q0, Senkunden.pin1
  N27: Vin.pin2, Bauteil1.VIN
  N28: Bauteil1.D12/MISO, Tick_Taster.pin2
  N29: Bauteil1.A5, ZS-042_RTC1.SCL
  N30: Bauteil1.A4, ZS-042_RTC1.SDA
  N31: Bauteil1.D13/SCK, Tick_Taster.pin1

notes:
  Stunden
  Minuten
  Sekunden
